# Fritzing sketch multi_VL53L0X_schematic (saved by Fritzing 0.9.3b)
breadboards: 1

parts:
  Part1 = Arduino Nano (Rev3.0)
  Part2 = Adafruit VL53L0X Time of Flight Distance Sensor [part_number="Adafruit #3317"]
  Part3 = Adafruit VL53L0X Time of Flight Distance Sensor [part_number="Adafruit #3317"]
  Part4 = Adafruit VL53L0X Time of Flight Distance Sensor [part_number="Adafruit #3317"]
  Part5 = Adafruit VL53L0X Time of Flight Distance Sensor [part_number="Adafruit #3317"]

nets:
  N1: Part1.D4, Part3.XSHUT
  N2: Part1.D5, Part2.XSHUT
  N3: Part1.D6, Part4.XSHUT
  N4: Part1.D7, Part5.XSHUT
  GND: Part1.GND, Part2.GND, Part3.GND, Part4.GND, Part5.GND
  5V: Part1.5V, Part2.VIN, Part3.VIN, Part4.VIN, Part5.VIN
  N5: Part1.A5, Part2.SCL, Part3.SCL, Part4.SCL, Part5.SCL
  N6: Part1.A4, Part2.SDA, Part3.SDA, Part4.SDA, Part5.SDA

custom parts:
  Adafruit VL53L0X Time of Flight Distance Sensor: The VL53L0X is a Time of Flight distance sensor like no other you've used! The sensor contains a very tiny invisible laser source, and a matching sensor. The VL53L0X can detect the "time of flight", or how long the light has taken to bounce back to the sensor. Since it uses a very narrow light source, it is good for determining distance of only the surface directly in front of it. Unlike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
